# Fritzing sketch Triac (Lamp dimmer) (saved by Fritzing 0.7.4b)
perfboards: 1

parts:
  LOAD = Screw terminal - 2 pins [package=THT]
  220 = Screw terminal - 2 pins [package=THT]
  MOC3061 = Optocoupler [package=THT]
  R2 = Resistor [tolerance=±5% resistance=470 package=THT]
  GND = female pin header, 2 pins [form="♀ (female)"]
  BT137 = BTA Triac [part_number=BT137 package="TO220 [THT]"]
  R1 = Resistor [tolerance=±5% resistance=220 package=THT]
  S1 = Reed switch [package=THT]

nets:
  N1: LOAD.pin1, BT137.A2, R1.Pin_0
  N2: LOAD.pin2, 220.pin1
  N3: 220.pin2, S1.pin_2
  N4: MOC3061.Pin_1, R2.Pin_0
  GND: MOC3061.Pin_2, GND.pin1
  N5: MOC3061.Pin_6, R1.Pin_1
  N6: MOC3061.Pin_4, BT137.G
  N7: R2.Pin_1, GND.pin2
  N8: BT137.A1, S1.pin_1

notes:
  PWM

custom parts:
  Optocoupler: Optoisolator Zero-Cross Triac Driver
  BTA Triac: BTA16
